# Fritzing sketch FirstSketch (saved by Fritzing 0.9.3b)
breadboards: 1

parts:
  Pico1 = rpi_pico
  LED1 = LED - 5mm [color="Red (633nm)" package="5 mm [THT]"]
  R1 = Resistor [tolerance=±5% resistance=220 package=THT]

nets:
  N1: Pico1.connector3, R1.Pin_1
  N2: Pico1.connector43, LED1.anode
  N3: LED1.cathode, R1.Pin_0
